// Digital circuit branch.dig as structural Verilog
module branch (
  input  [2:0] WS,
  input  WE,
  output BT
);

  wire nor_1_out;
  wire [2:0] xor_1_out;

  assign xor_1_out = 3'b111 ^ WS;  // XOr xor_1, 3 bits wide
  nor nor_1 (nor_1_out, xor_1_out[0], xor_1_out[1], xor_1_out[2]);
  and and_1 (BT, nor_1_out, WE);
endmodule

/* Test case BT:
WS     WE  BT
000    X   0
001    X   0
010    X   0
011    X   0
100    X   0
101    X   0
110    X   0
111    1   1
111    0   0
*/
