// Digital circuit control_unit.dig as structural Verilog
module control_unit (
  input  [15:0] INST,
  input  ZERO,
  output [1:0] ALUOP,
  output [2:0] RS1,
  output [2:0] RS2,
  output [2:0] WS,
  output STR,
  output WE,
  output [1:0] DMUX,
  output LDR,
  output FLEN,
  output EXEC
);

  wire and_1_out, not_1_out, not_2_out, not_3_out, not_5_out, or_2_out;
  wire [1:1] not_4_out;

  not not_1 (not_1_out, INST[11]);
  not not_2 (not_2_out, INST[13]);
  not not_3 (not_3_out, INST[14]);
  not not_4 (not_4_out[1], INST[15]);
  Multiplexer #(.Bits(2)) multiplexer_1 (
    .sel(not_3_out), .in_0(INST[15:14]), .in_1({not_4_out[1], INST[14]}), .out(DMUX));
  or or_1 (EXEC, ZERO, not_1_out);
  not not_5 (not_5_out, INST[12]);
  or or_2 (or_2_out, INST[12], INST[13], not_3_out, INST[15]);
  and and_1 (and_1_out, not_5_out, not_2_out, INST[14], not_4_out[1]);
  and and_2 (LDR, INST[12], not_2_out, INST[14], not_4_out[1]);
  Multiplexer #(.Bits(3)) multiplexer_2 (.sel(INST[15]), .in_0(INST[10:8]), .in_1(INST[2:0]), .out(RS2));
  Multiplexer multiplexer_3 (.sel(EXEC), .in_0(1'b0), .in_1(and_1_out), .out(STR));
  Multiplexer multiplexer_4 (.sel(EXEC), .in_0(1'b0), .in_1(or_2_out), .out(WE));
  Multiplexer multiplexer_5 (.sel(EXEC), .in_0(1'b0), .in_1(INST[15]), .out(FLEN));

  assign ALUOP = INST[13:12];
  assign RS1 = INST[6:4];
  assign WS = INST[10:8];

  // Notes on the sheet:
  //   opcode
  //   Z
  //   Rd
  //   Ra
  //   Rb
endmodule

/* Test case All Tests:
	INST                                    WE  ALUOP  RS1   RS2  WS  STR  LDR DMUX FLEN

let aluop  = 0b1000;
let ldrop  = 0b0101;
let strop  = 0b0100;
let movlop = 0b0000;

loop(rd, 1<<3)
loop(ra, 1<<3)
loop(rb, 1<<3)

loop(i, 4)
	((aluop+i)<<12 | rd<<8 | ra<<4 | rb<<0) 1  (i)     (ra)  (rb) (rd)  0   X    0     1  #test add/sub/and/orr
end loop

	(ldrop    <<12 | rd<<8 | ra<<4 )        1  X       (ra)  x    (rd)  0   1    1     0  #test ldr
	(strop    <<12 | rd<<8 | ra<<4 )        0  X       (ra)  (rd)  X    1   X    X     0  #test str
	
	let imm = random(256);
	(movlop   <<12 | rd<<8 | imm )          1  X       X      X   (rd)  0   X    2     0  #test movl

end loop
end loop
end loop
*/

/* Test case NOP:
	INST                                           ZERO NOP EXEC

let aluop  = 0b1000;
let ldrop  = 0b0101;
let strop  = 0b0100;
let movlop = 0b0000;

loop(rd, 1<<3)
loop(ra, 1<<3)
loop(rb, 1<<3)

loop(i, 4)
	((aluop+i)<<12 | 1<<11 | rd<<8 | ra<<4 | rb<<0)  1   1  0 #test add/sub/and/orr
        ((aluop+i)<<12 | 1<<11 | rd<<8 | ra<<4 | rb<<0)  1   0  1
	((aluop+i)<<12 | 1<<11 | rd<<8 | ra<<4 | rb<<0)  0   1  0
	((aluop+i)<<12 | 1<<11 | rd<<8 | ra<<4 | rb<<0)  0   0  0
	((aluop+i)<<12 | 0<<11 | rd<<8 | ra<<4 | rb<<0)  X   1  0 
	((aluop+i)<<12 | 0<<11 | rd<<8 | ra<<4 | rb<<0)  X   0  1
end loop

	(ldrop    <<12 | 1<<11 | rd<<8 | ra<<4 )  	 1   1  0 #test ldr
        (ldrop    <<12 | 1<<11 | rd<<8 | ra<<4 )  	 1   0  1
	(ldrop    <<12 | 1<<11 | rd<<8 | ra<<4 )  	 0   1  0
	(ldrop    <<12 | 1<<11 | rd<<8 | ra<<4 )  	 0   0  0
	(ldrop    <<12 | 0<<11 | rd<<8 | ra<<4 )  	 X   1  0 
	(ldrop    <<12 | 0<<11 | rd<<8 | ra<<4 )  	 X   0  1

	(strop    <<12 | 1<<11 | rd<<8 | ra<<4 )  	 1   1  0 #test str
        (strop    <<12 | 1<<11 | rd<<8 | ra<<4 )  	 1   0  1
	(strop    <<12 | 1<<11 | rd<<8 | ra<<4 )  	 0   1  0
	(strop    <<12 | 1<<11 | rd<<8 | ra<<4 )  	 0   0  0
	(strop    <<12 | 0<<11 | rd<<8 | ra<<4 )  	 X   1  0 
	(strop    <<12 | 0<<11 | rd<<8 | ra<<4 )  	 X   0  1
	
	let imm = random(256);
	(movlop   <<12 | 1<<11 | rd<<8 | imm )  	 1   1  0 #test movl
        (movlop   <<12 | 1<<11 | rd<<8 | imm )  	 1   0  1
	(movlop   <<12 | 1<<11 | rd<<8 | imm )  	 0   1  0
	(movlop   <<12 | 1<<11 | rd<<8 | imm )  	 0   0  0
	(movlop   <<12 | 0<<11 | rd<<8 | imm )  	 X   1  0 
	(movlop   <<12 | 0<<11 | rd<<8 | imm )  	 X   0  1

end loop
end loop
end loop
*/

/* Test case EXEC:
	INST                                           ZERO   EXEC 

let aluop  = 0b1000;
let ldrop  = 0b0101;
let strop  = 0b0100;
let movlop = 0b0000;

loop(rd, 1<<3)
loop(ra, 1<<3)
loop(rb, 1<<3)

loop(i, 4)
	((aluop+i)<<12 | 1<<11 | rd<<8 | ra<<4 | rb<<0)  1      1    #test add/sub/and/orr
	((aluop+i)<<12 | 1<<11 | rd<<8 | ra<<4 | rb<<0)  0      0 
	((aluop+i)<<12 | 0<<11 | rd<<8 | ra<<4 | rb<<0)  X      1   
end loop

	(ldrop    <<12 | 1<<11 | rd<<8 | ra<<4 )         1      1    #test ldr
	(ldrop    <<12 | 1<<11 | rd<<8 | ra<<4 )         0      0
	(ldrop    <<12 | 0<<11 | rd<<8 | ra<<4 )         X      1  

	(strop    <<12 | 1<<11 | rd<<8 | ra<<4 )         1      1     #test str
	(strop    <<12 | 1<<11 | rd<<8 | ra<<4 )         0      0
	(strop    <<12 | 0<<11 | rd<<8 | ra<<4 )         X      1 

	
	let imm = random(256);
	(movlop   <<12 | 1<<11 | rd<<8 | imm )           1      1    #test movl
	(movlop   <<12 | 1<<11 | rd<<8 | imm )           0      0 
	(movlop   <<12 | 0<<11 | rd<<8 | imm )           X      1 

end loop
end loop
end loop
*/

/* Test case WS:
	INST                                    WS 

let aluop  = 0b1000;
let ldrop  = 0b0101;
let strop  = 0b0100;
let movlop = 0b0000;

loop(rd, 1<<3)
loop(ra, 1<<3)
loop(rb, 1<<3)

loop(i, 4)
	((aluop+i)<<12 | rd<<8 | ra<<4 | rb<<0) (rd)  #test add/sub/and/orr
end loop

	(ldrop    <<12 | rd<<8 | ra<<4 )        (rd)   #test ldr
	(strop    <<12 | rd<<8 | ra<<4 )        X     #test str
	
	let imm = random(256);
	(movlop   <<12 | rd<<8 | imm )          (rd)  #test movl

end loop
end loop
end loop
*/

/* Test case RS1:
	INST                                    RS1  

let aluop  = 0b1000;
let ldrop  = 0b0101;
let strop  = 0b0100;
let movlop = 0b0000;

loop(rd, 1<<3)
loop(ra, 1<<3)
loop(rb, 1<<3)

loop(i, 4)
	((aluop+i)<<12 | rd<<8 | ra<<4 | rb<<0) (ra)  #test add/sub/and/orr
end loop

	(ldrop    <<12 | rd<<8 | ra<<4 )        (ra)  #test ldr
	(strop    <<12 | rd<<8 | ra<<4 )        (ra)  #test str

end loop
end loop
end loop
*/

/* Test case RS2:
	INST                                    RS2  

let aluop  = 0b1000;
let ldrop  = 0b0101;
let strop  = 0b0100;
let movlop = 0b0000;

loop(rd, 1<<3)
loop(ra, 1<<3)
loop(rb, 1<<3)

loop(i, 4)
	((aluop+i)<<12 | rd<<8 | ra<<4 | rb<<0) (rb) #test add/sub/and/orr
end loop
	(strop    <<12 | rd<<8 | ra<<4 )        (rd) #test str

end loop
end loop
end loop
*/

/* Test case STR:
	INST                                    STR 

let aluop  = 0b1000;
let ldrop  = 0b0101;
let strop  = 0b0100;
let movlop = 0b0000;

loop(rd, 1<<3)
loop(ra, 1<<3)
loop(rb, 1<<3)

loop(i, 4)
	((aluop+i)<<12 | rd<<8 | ra<<4 | rb<<0) 0  #test add/sub/and/orr
end loop

	(ldrop    <<12 | rd<<8 | ra<<4 )        0  #test ldr
	(strop    <<12 | rd<<8 | ra<<4 )        1  #test str
	
	let imm = random(256);
	(movlop   <<12 | rd<<8 | imm )          0  #test movl

end loop
end loop
end loop
*/

/* Test case WE:
	INST                                    WE  

let aluop  = 0b1000;
let ldrop  = 0b0101;
let strop  = 0b0100;
let movlop = 0b0000;

loop(rd, 1<<3)
loop(ra, 1<<3)
loop(rb, 1<<3)

loop(i, 4)
	((aluop+i)<<12 | rd<<8 | ra<<4 | rb<<0) 1  #test add/sub/and/orr
end loop

	(ldrop    <<12 | rd<<8 | ra<<4 )        1  #test ldr
	(strop    <<12 | rd<<8 | ra<<4 )        0  #test str
	
	let imm = random(256);
	(movlop   <<12 | rd<<8 | imm )          1  #test movl

end loop
end loop
end loop
*/

/* Test case LDR:
	INST                                    LDR 

let aluop  = 0b1000;
let ldrop  = 0b0101;
let strop  = 0b0100;
let movlop = 0b0000;

loop(rd, 1<<3)
loop(ra, 1<<3)
loop(rb, 1<<3)

loop(i, 4)
	((aluop+i)<<12 | rd<<8 | ra<<4 | rb<<0) X    #test add/sub/and/orr
end loop

	(ldrop    <<12 | rd<<8 | ra<<4 )        1    #test ldr
	(strop    <<12 | rd<<8 | ra<<4 )        X    #test str
	
	let imm = random(256);
	(movlop   <<12 | rd<<8 | imm )          X    #test movl

end loop
end loop
end loop
*/

/* Test case DMUX:
	INST                                    DMUX

let aluop  = 0b1000;
let ldrop  = 0b0101;
let strop  = 0b0100;
let movlop = 0b0000;

loop(rd, 1<<3)
loop(ra, 1<<3)
loop(rb, 1<<3)

loop(i, 4)
	((aluop+i)<<12 | rd<<8 | ra<<4 | rb<<0) 0  #test add/sub/and/orr
end loop

	(ldrop    <<12 | rd<<8 | ra<<4 )        1  #test ldr
	
	let imm = random(256);
	(movlop   <<12 | rd<<8 | imm )          2  #test movl

end loop
end loop
end loop
*/

/* Test case ALUOP:
	INST                                    ALUOP 

let aluop  = 0b1000;
let ldrop  = 0b0101;
let strop  = 0b0100;
let movlop = 0b0000;

loop(rd, 1<<3)
loop(ra, 1<<3)
loop(rb, 1<<3)

loop(i, 4)
	((aluop+i)<<12 | rd<<8 | ra<<4 | rb<<0) (i)    #test add/sub/and/orr
end loop

end loop
end loop
end loop
*/

/* Test case FLEN:
	INST                                      	ZERO   FLEN 

let aluop  = 0b1000;
let ldrop  = 0b0101;
let strop  = 0b0100;
let movlop = 0b0000;

loop(rd, 1<<3)
loop(ra, 1<<3)
loop(rb, 1<<3)

loop(i, 4)
	((aluop+i)<<12 | 1<<11 | rd<<8 | ra<<4 | rb<<0)  1     1   #test add/sub/and/orr
	((aluop+i)<<12 | 1<<11 | rd<<8 | ra<<4 | rb<<0)  0     0 
	((aluop+i)<<12 | 0<<11 | rd<<8 | ra<<4 | rb<<0)  X     1
end loop

	(ldrop    <<12 | rd<<8 | ra<<4 )        	 X     0 #test ldr
	(strop    <<12 | rd<<8 | ra<<4 )        	 X     0 #test str
	
	let imm = random(256);
	(movlop   <<12 | rd<<8 | imm )          	 X     0 #test movl

end loop
end loop
end loop
*/
