// Digital circuit forwarding.dig as structural Verilog
module forwarding (
  input  [2:0] ID_EX_RS1,
  input  [2:0] ID_EX_RS2,
  input  [2:0] EX_WB_WS,
  input  EX_WB_WE,
  output ALU1,
  output ALU2
);

  wire nor_1_out, nor_2_out;
  wire [2:0] xor_1_out, xor_2_out;

  assign xor_1_out = EX_WB_WS ^ ID_EX_RS1;  // XOr xor_1, 3 bits wide
  assign xor_2_out = EX_WB_WS ^ ID_EX_RS2;  // XOr xor_2, 3 bits wide
  nor nor_1 (nor_1_out, xor_1_out[0], xor_1_out[1], xor_1_out[2]);
  nor nor_2 (nor_2_out, xor_2_out[0], xor_2_out[1], xor_2_out[2]);
  and and_1 (ALU1, EX_WB_WE, nor_1_out);
  and and_2 (ALU2, EX_WB_WE, nor_2_out);
endmodule

/* Test case FORWARD:
EX/WB.WE    EX/WB.WS    ID/EX.RS1   ID/EX.RS2    ALU1   ALU2

loop(a, 1<<3)
let b = a+1;
1           (a)          (a)          (a)         1      1
0           (a)          (a)          (a)         0      0
1           (a)          (a)          (b)         1      0
1           (a)          (b)          (a)         0      1
1           (a)          (b)          (b)         0      0
end loop
*/
