// Digital circuit mem.dig as structural Verilog
module mem (
  input  STR,
  input  [15:0] _1A,
  input  [15:0] _2A,
  output NC
);

  wire nor_1_out;
  wire [15:0] xor_1_out;

  assign xor_1_out = _1A ^ _2A;  // XOr xor_1, 16 bits wide
  nor nor_1 (nor_1_out, xor_1_out[0], xor_1_out[1], xor_1_out[2], xor_1_out[3], xor_1_out[4], xor_1_out[5], xor_1_out[6], xor_1_out[7], xor_1_out[8], xor_1_out[9], xor_1_out[10], xor_1_out[11], xor_1_out[12], xor_1_out[13], xor_1_out[14], xor_1_out[15]);
  and and_1 (NC, STR, nor_1_out);
endmodule

/* Test case NC:
STR   1A     2A    NOP

loop (i, 1000)

let a = random(1<<16);
let b = a-1;
1     (a)    (a)    1
1     (a)    (b)    0
0     (a)    (a)    0
0     (a)    (b)    0
end loop
*/
