// Digital circuit reg_file.dig as structural Verilog
module reg_file (
  input  [2:0] RS1,
  input  [2:0] RS2,
  input  [2:0] WS,
  input  WE,
  input  [15:0] IN,
  input  clk,
  input  FLEN,
  input  [3:0] FLAG,
  input  NC,
  output [15:0] OUT1,
  output [15:0] OUT2,
  output [15:0] PC,
  output ZERO
);

  wire demultiplexer_1_out_0, demultiplexer_1_out_1, demultiplexer_1_out_2, demultiplexer_1_out_3,
       demultiplexer_1_out_4, demultiplexer_1_out_7, multiplexer_2_out, not_1_out, not_2_out,
       notconnected_4_out;
  wire [15:0] multiplexer_1_out, notconnected_1_out, notconnected_2_out, notconnected_3_out, plus_1_s, R1_q,
       R2_q, R3_q, R4_q, ramdualport_1_d, register_1_q, register_2_q, RZ_q;
  wire [15:1] FL_q;

  Demultiplexer #(.Selector_Bits(3)) demultiplexer_1 (
    .sel(WS), .in(WE), .out_0(demultiplexer_1_out_0), .out_1(demultiplexer_1_out_1),
    .out_2(demultiplexer_1_out_2), .out_3(demultiplexer_1_out_3), .out_4(demultiplexer_1_out_4),
    .out_7(demultiplexer_1_out_7));  // open: out_5, out_6
  // Probe NC on NC
  Multiplexer #(.Bits(16)) multiplexer_1 (
    .sel(demultiplexer_1_out_7), .in_0(plus_1_s), .in_1(IN), .out(multiplexer_1_out));
  Multiplexer multiplexer_2 (.sel(NC), .in_0(1'b1), .in_1(1'b0), .out(multiplexer_2_out));
  Register #(.Bits(16)) RZ (.D({16{1'b0}}), .C(clk), .en(demultiplexer_1_out_0), .Q(RZ_q));
  Register #(.Bits(16)) R1 (.D(IN), .C(clk), .en(demultiplexer_1_out_1), .Q(R1_q));
  Register #(.Bits(16)) R2 (.D(IN), .C(clk), .en(demultiplexer_1_out_2), .Q(R2_q));
  Register #(.Bits(16)) R3 (.D(IN), .C(clk), .en(demultiplexer_1_out_3), .Q(R3_q));
  Register #(.Bits(16)) R4 (.D(IN), .C(clk), .en(demultiplexer_1_out_4), .Q(R4_q));
  Register #(.Bits(16)) FL (.D({{12{1'b0}}, FLAG}), .C(clk), .en(FLEN), .Q({FL_q, ZERO}));
  Register #(.Bits(16)) u_PC (.D(multiplexer_1_out), .C(clk), .en(multiplexer_2_out), .Q(PC));
  Add #(.Bits(16)) plus_1 (.a(16'h1), .b(PC), .c_i(1'b0), .s(plus_1_s));  // open: c_o
  Multiplexer #(.Selector_Bits(3), .Bits(16)) multiplexer_3 (
    .sel(RS1), .in_0(RZ_q), .in_1(R1_q), .in_2(R2_q), .in_3(R3_q), .in_4(R4_q), .in_5({FL_q, ZERO}),
    .in_6(notconnected_1_out), .in_7(PC), .out(OUT1));
  // NotConnected on notconnected_1_out
  Multiplexer #(.Selector_Bits(3), .Bits(16)) multiplexer_4 (
    .sel(RS2), .in_0(RZ_q), .in_1(R1_q), .in_2(R2_q), .in_3(R3_q), .in_4(R4_q), .in_5({FL_q, ZERO}),
    .in_6(notconnected_2_out), .in_7(PC), .out(OUT2));
  // NotConnected on notconnected_2_out
  not not_1 (not_1_out, clk);
  not not_2 (not_2_out, clk);
  // NotConnected on notconnected_3_out
  // NotConnected on notconnected_4_out
  Register #(.Bits(16)) register_1 (.D(OUT1), .C(not_1_out), .en(1'b1), .Q(register_1_q));
  RAMDualPort #(.AddrBits(16), .Bits(16)) ramdualport_1 (
    .A(PC), .Din(notconnected_3_out), .str(notconnected_4_out), .C(clk), .ld(1'b1), .D(ramdualport_1_d));
  // Probe PPR on register_1_q
  // Probe MEM on ramdualport_1_d
  Register #(.Bits(16)) register_2 (.D(ramdualport_1_d), .C(not_2_out), .en(1'b1), .Q(register_2_q));
  // Probe IF/ID on register_2_q

  // Notes on the sheet:
  //   RS1: The index of the register which should output its value to OUT1.
  //   RS2: The index of the register which should output its value to OUT2.
  //   WS: The index of the register which should save the value on IN on the next clock cycle (if WE is high).
  //   WE: Whether the register selected by WS should save the value from IN on the next cycle.
  //   IN: The value to be saved into the register specified by WS if WE is high,
  //   OUT1: The value in the register specified by RS1.
  //   OUT2: The value in the register specified by RS2.
  //   FLEN: Whether the flag register needs to be updated
endmodule

/* Test case RF:
clk RS1 RS2 WS  WE   IN     OUT1   OUT2  FLAG FLEN NO-OP PC_
c    0   0  0   1   0x1234 0x0000 0x0000  X    X    1    0
c    1   0  1   1   0xBEEF 0xBEEF 0x0000  X    X    1    0
c    2   1  2   1   0xDEAD 0xDEAD 0xBEEF  X    X    1    0
c    3   2  3   1   0xFFFF 0xFFFF 0xDEAD  X    X    1    0
c    3   2  3   0   0xABCD 0xFFFF 0xDEAD  X    X    1    0
c    3   2  2   0   0xABCD 0xFFFF 0xDEAD  X    X    1    0
c    1   0  1   0   0xABCD 0xBEEF 0x0000  X    X    1    0
c    1   0  0   0   0xABCD 0xBEEF 0x0000  X    X    1    0
c    1   0  2   1   0xBADE 0xBEEF 0x0000  X    X    1    0
c    0   2  2   1   0xBADE 0x0000 0xBADE  X    X    1    0
c    0   0  2   0   0x1234 0x0000 0x0000  X    X    1    0
c    2   3  0   1   0x0000 0xBADE 0xFFFF  X    X    1    0
c    0   0  2   0   0x1234 0x0000 0x0000  X    X    1    0
   

loop(flag, 1<<4)
	let in = random(1<<16);
c    5   5  X   X   (in)   (flag) (flag) (flag) 1    1   0
c    5   5  X   X   (in)   (flag) (flag) (flag) 0    1   0
end loop 
*/
