// Digital circuit cpu.dig as structural Verilog
module cpu (
  input  CLK
);

  wire control_unit_1_exec, control_unit_1_flen, control_unit_1_ldr, control_unit_1_str, control_unit_1_we,
       reg_file_1_zero;
  wire [1:0] control_unit_1_aluop, control_unit_1_dmux;
  wire [2:0] control_unit_1_rs1, control_unit_1_rs2, control_unit_1_ws;
  wire [3:0] alu_1_flag;
  wire [7:0] RAM_d2;
  wire [15:0] alu_1_result, and_1_out, multiplexer_1_out, multiplexer_2_out, notconnected_1_out, or_1_out,
       RAM_d1, reg_file_1_out1, reg_file_1_out2, reg_file_1_pc;
  wire [15:8] RAM_d2_2;

  assign and_1_out = 16'hff & reg_file_1_out2;  // And and_1, 16 bits wide
  control_unit control_unit_1 (
    .INST({RAM_d2_2, RAM_d2}), .ZERO(reg_file_1_zero), .ALUOP(control_unit_1_aluop),
    .RS1(control_unit_1_rs1), .RS2(control_unit_1_rs2), .WS(control_unit_1_ws), .STR(control_unit_1_str),
    .WE(control_unit_1_we), .DMUX(control_unit_1_dmux), .LDR(control_unit_1_ldr), .FLEN(control_unit_1_flen),
    .EXEC(control_unit_1_exec));
  assign or_1_out = {RAM_d2, {8{1'b0}}} | and_1_out;  // Or or_1, 16 bits wide
  LED led_1 (.in(control_unit_1_exec));
  Multiplexer #(.Bits(16)) multiplexer_1 (
    .sel(RAM_d2_2[12]), .in_0({{8{1'b0}}, RAM_d2}), .in_1(or_1_out), .out(multiplexer_1_out));
  Multiplexer #(.Selector_Bits(2), .Bits(16)) multiplexer_2 (
    .sel(control_unit_1_dmux), .in_0(alu_1_result), .in_1(RAM_d1), .in_2(multiplexer_1_out),
    .in_3(notconnected_1_out), .out(multiplexer_2_out));
  // NotConnected on notconnected_1_out
  // Probe DATA on multiplexer_2_out
  reg_file reg_file_1 (
    .RS1(control_unit_1_rs1), .RS2(control_unit_1_rs2), .WS(control_unit_1_ws), .WE(control_unit_1_we),
    .IN(multiplexer_2_out), .clk(CLK), .FLEN(control_unit_1_flen), .FLAG(alu_1_flag), .OUT1(reg_file_1_out1),
    .OUT2(reg_file_1_out2), .PC(reg_file_1_pc), .ZERO(reg_file_1_zero));
  alu alu_1 (
    .A(reg_file_1_out1), .B(reg_file_1_out2), .ALUOP(control_unit_1_aluop), .RESULT(alu_1_result),
    .FLAG(alu_1_flag));
  RAMDualAccess #(.AddrBits(16), .isProgramMemory("true"), .Bits(16)) RAM (
    .str(control_unit_1_str), .C(CLK), .ld(control_unit_1_ldr), .A1(reg_file_1_out1), .Din1(reg_file_1_out2),
    .A2(reg_file_1_pc), .D1(RAM_d1), .D2({RAM_d2_2, RAM_d2}));
endmodule
